// Logisim project phase1.3.circ as structural Verilog
module main (
);

  wire alu_1_branch, ALUsrc, clock_1_out, JALR, MemRead, MemToReg, MemWrite, RegW, SSET, undriven_2;
  wire [1:0] PCSrc;
  wire [4:0] instruction_memory_1_out_4, instruction_memory_1_out_5, instruction_memory_1_out_6,
       multiplexer_1_out;
  wire [5:0] instruction_memory_1_out_7;
  wire [10:0] instruction_memory_1_out_2;
  wire [11:0] alu_1_result_2, alucontrol_1_aluop;
  wire [19:0] alu_1_result, undriven;
  wire [31:0] data_memory_1_out_6, extendunit_1_out_3, multiplexer_2_out, multiplexer_3_out,
       multiplexer_4_out, multiplexer_5_out, shifter_1_out, undriven_3, undriven_4, undriven_5;

  PC pc_1 (
    .ImmL5(instruction_memory_1_out_6), .NextPC32(undriven_3), .PC20(undriven), .JALRPC(alu_1_result),
    .PCSrc(PCSrc), .Clock(clock_1_out), .ImmU11(instruction_memory_1_out_2));
  Clock clock_1 (.out(clock_1_out));
  instruction_memory instruction_memory_1 (
    .in_1(undriven), .out_2(instruction_memory_1_out_2[10:5]), .out_3(instruction_memory_1_out_2[4:0]),
    .out_4(instruction_memory_1_out_4), .out_5(instruction_memory_1_out_5),
    .out_6(instruction_memory_1_out_6), .out_7(instruction_memory_1_out_7));
  ALUcontrol alucontrol_1 (
    .func({instruction_memory_1_out_2[4:0], instruction_memory_1_out_2[10:5]}),
    .OPcode(instruction_memory_1_out_7), .ALUop(alucontrol_1_aluop));
  Multiplexer #(.width(5)) multiplexer_1 (
    .in0(instruction_memory_1_out_5), .in1(instruction_memory_1_out_6), .out(multiplexer_1_out),
    .sel(undriven_2));
  ExtendUnit extendunit_1 (
    .in_2({instruction_memory_1_out_2, instruction_memory_1_out_4}), .ExtendOp(SSET),
    .out_3(extendunit_1_out_3));
  regFile regfile_1 (
    .RegWrite(RegW), .clock(clock_1_out), .RA(multiplexer_1_out), .Busw(multiplexer_2_out),
    .RB(instruction_memory_1_out_4), .BusA(undriven_5), .BusB(undriven_4), .RW(instruction_memory_1_out_6));
  Multiplexer #(.width(32)) multiplexer_2 (
    .in0(multiplexer_5_out), .in1(undriven_3), .out(multiplexer_2_out), .sel(JALR));
  Shifter #(.width(32)) shifter_1 (.in(undriven_5), .\dist (5'b10000), .out(shifter_1_out));
  Multiplexer #(.width(32)) multiplexer_3 (.in0(undriven_5), .in1(shifter_1_out), .out(multiplexer_3_out), .sel(SSET));
  Multiplexer #(.width(32)) multiplexer_4 (
    .in0(undriven_4), .in1(extendunit_1_out_3), .out(multiplexer_4_out), .sel(ALUsrc));
  ALU alu_1 (
    .ALUop(alucontrol_1_aluop), .A(multiplexer_3_out), .B(multiplexer_4_out),
    .Result({alu_1_result_2, alu_1_result}), .Branch(alu_1_branch));
  data_memory data_memory_1 (
    .in_1(alu_1_result), .in_2(undriven_4), .in_3(MemWrite), .in_4(MemRead), .in_5(clock_1_out),
    .out_6(data_memory_1_out_6));
  Multiplexer #(.width(32)) multiplexer_5 (
    .in0({alu_1_result_2, alu_1_result}), .in1(data_memory_1_out_6), .out(multiplexer_5_out), .sel(MemToReg));
endmodule

module regFile (
  input  [4:0] RB,
  input  [4:0] RA,
  input  [4:0] RW,
  input  [31:0] BusB,
  input  [31:0] BusA,
  input  RegWrite,
  input  clock,
  input  [31:0] Busw
);

  wire and_1_out, and_2_out, and_3_out, and_4_out, and_5_out, and_6_out, and_7_out, and_8_out, and_9_out,
       and_10_out, and_11_out, and_12_out, and_13_out, and_14_out, and_15_out, and_16_out, and_17_out,
       and_18_out, and_19_out, and_20_out, and_21_out, and_22_out, and_23_out, and_24_out, and_25_out,
       and_26_out, and_27_out, and_28_out, and_29_out, and_30_out, and_31_out, decoder_1_out1,
       decoder_1_out2, decoder_1_out3, decoder_1_out4, decoder_1_out5, decoder_1_out6, decoder_1_out7,
       decoder_1_out8, decoder_1_out9, decoder_1_out10, decoder_1_out11, decoder_1_out12, decoder_1_out13,
       decoder_1_out14, decoder_1_out15, decoder_1_out16, decoder_1_out17, decoder_1_out18, decoder_1_out19,
       decoder_1_out20, decoder_1_out21, decoder_1_out22, decoder_1_out23, decoder_1_out24, decoder_1_out25,
       decoder_1_out26, decoder_1_out27, decoder_1_out28, decoder_1_out29, decoder_1_out30, decoder_1_out31,
       decoder_2_out0, decoder_2_out1, decoder_2_out2, decoder_2_out3, decoder_2_out4, decoder_2_out5,
       decoder_2_out6, decoder_2_out7, decoder_2_out8, decoder_2_out9, decoder_2_out10, decoder_2_out11,
       decoder_2_out12, decoder_2_out13, decoder_2_out14, decoder_2_out15, decoder_2_out16, decoder_2_out17,
       decoder_2_out18, decoder_2_out19, decoder_2_out20, decoder_2_out21, decoder_2_out22, decoder_2_out23,
       decoder_2_out24, decoder_2_out25, decoder_2_out26, decoder_2_out27, decoder_2_out28, decoder_2_out29,
       decoder_2_out30, decoder_2_out31, decoder_3_out0, decoder_3_out1, decoder_3_out2, decoder_3_out3,
       decoder_3_out4, decoder_3_out5, decoder_3_out6, decoder_3_out7, decoder_3_out8, decoder_3_out9,
       decoder_3_out10, decoder_3_out11, decoder_3_out12, decoder_3_out13, decoder_3_out14, decoder_3_out15,
       decoder_3_out16, decoder_3_out17, decoder_3_out18, decoder_3_out19, decoder_3_out20, decoder_3_out21,
       decoder_3_out22, decoder_3_out23, decoder_3_out24, decoder_3_out25, decoder_3_out26, decoder_3_out27,
       decoder_3_out28, decoder_3_out29, decoder_3_out30, decoder_3_out31;
  wire [31:0] controlled_buffer_1_out, controlled_buffer_33_out, register_1_q, register_2_q, register_3_q,
       register_4_q, register_5_q, register_6_q, register_7_q, register_8_q, register_9_q, register_10_q,
       register_11_q, register_12_q, register_13_q, register_14_q, register_15_q, register_16_q,
       register_17_q, register_18_q, register_19_q, register_20_q, register_21_q, register_22_q,
       register_23_q, register_24_q, register_25_q, register_26_q, register_27_q, register_28_q,
       register_29_q, register_30_q, register_31_q, undriven;

  Decoder #(.enable("false"), .select(5)) decoder_1 (
    .out1(decoder_1_out1), .out2(decoder_1_out2), .out3(decoder_1_out3), .out4(decoder_1_out4),
    .out5(decoder_1_out5), .out6(decoder_1_out6), .out7(decoder_1_out7), .out8(decoder_1_out8),
    .out9(decoder_1_out9), .out10(decoder_1_out10), .out11(decoder_1_out11), .out12(decoder_1_out12),
    .out13(decoder_1_out13), .out14(decoder_1_out14), .out15(decoder_1_out15), .out16(decoder_1_out16),
    .out17(decoder_1_out17), .out18(decoder_1_out18), .out19(decoder_1_out19), .out20(decoder_1_out20),
    .out21(decoder_1_out21), .out22(decoder_1_out22), .out23(decoder_1_out23), .out24(decoder_1_out24),
    .out25(decoder_1_out25), .out26(decoder_1_out26), .out27(decoder_1_out27), .out28(decoder_1_out28),
    .out29(decoder_1_out29), .out30(decoder_1_out30), .out31(decoder_1_out31), .sel(RW));  // open: out0
  Register #(.width(32)) register_1 (.D(undriven), .en(and_1_out), .clk(clock), .Q(register_1_q));  // open: clr
  and and_1 (and_1_out, decoder_1_out1, RegWrite);
  Register #(.width(32)) register_2 (.D(undriven), .en(and_2_out), .clk(clock), .Q(register_2_q));  // open: clr
  and and_2 (and_2_out, decoder_1_out2, RegWrite);
  Register #(.width(32)) register_3 (.D(undriven), .en(and_3_out), .clk(clock), .Q(register_3_q));  // open: clr
  and and_3 (and_3_out, decoder_1_out3, RegWrite);
  Register #(.width(32)) register_4 (.D(undriven), .en(and_4_out), .clk(clock), .Q(register_4_q));  // open: clr
  and and_4 (and_4_out, decoder_1_out4, RegWrite);
  Register #(.width(32)) register_5 (.D(undriven), .en(and_5_out), .clk(clock), .Q(register_5_q));  // open: clr
  and and_5 (and_5_out, decoder_1_out5, RegWrite);
  Register #(.width(32)) register_6 (.D(undriven), .en(and_6_out), .clk(clock), .Q(register_6_q));  // open: clr
  and and_6 (and_6_out, decoder_1_out6, RegWrite);
  Register #(.width(32)) register_7 (.D(undriven), .en(and_7_out), .clk(clock), .Q(register_7_q));  // open: clr
  and and_7 (and_7_out, decoder_1_out7, RegWrite);
  Register #(.width(32)) register_8 (.D(undriven), .en(and_8_out), .clk(clock), .Q(register_8_q));  // open: clr
  and and_8 (and_8_out, decoder_1_out8, RegWrite);
  Register #(.width(32)) register_9 (.D(undriven), .en(and_9_out), .clk(clock), .Q(register_9_q));  // open: clr
  and and_9 (and_9_out, decoder_1_out9, RegWrite);
  Register #(.width(32)) register_10 (.D(undriven), .en(and_10_out), .clk(clock), .Q(register_10_q));  // open: clr
  and and_10 (and_10_out, decoder_1_out10, RegWrite);
  Register #(.width(32)) register_11 (.D(undriven), .en(and_11_out), .clk(clock), .Q(register_11_q));  // open: clr
  and and_11 (and_11_out, decoder_1_out11, RegWrite);
  Register #(.width(32)) register_12 (.D(undriven), .en(and_12_out), .clk(clock), .Q(register_12_q));  // open: clr
  and and_12 (and_12_out, decoder_1_out12, RegWrite);
  Register #(.width(32)) register_13 (.D(undriven), .en(and_13_out), .clk(clock), .Q(register_13_q));  // open: clr
  and and_13 (and_13_out, decoder_1_out13, RegWrite);
  Register #(.width(32)) register_14 (.D(undriven), .en(and_14_out), .clk(clock), .Q(register_14_q));  // open: clr
  and and_14 (and_14_out, decoder_1_out14, RegWrite);
  Register #(.width(32)) register_15 (.D(undriven), .en(and_15_out), .clk(clock), .Q(register_15_q));  // open: clr
  and and_15 (and_15_out, decoder_1_out15, RegWrite);
  Register #(.width(32)) register_16 (.D(undriven), .en(and_16_out), .clk(clock), .Q(register_16_q));  // open: clr
  and and_16 (and_16_out, decoder_1_out16, RegWrite);
  Register #(.width(32)) register_17 (.D(undriven), .en(and_17_out), .clk(clock), .Q(register_17_q));  // open: clr
  and and_17 (and_17_out, decoder_1_out17, RegWrite);
  Register #(.width(32)) register_18 (.D(undriven), .en(and_18_out), .clk(clock), .Q(register_18_q));  // open: clr
  and and_18 (and_18_out, decoder_1_out18, RegWrite);
  Register #(.width(32)) register_19 (.D(undriven), .en(and_19_out), .clk(clock), .Q(register_19_q));  // open: clr
  and and_19 (and_19_out, decoder_1_out19, RegWrite);
  Register #(.width(32)) register_20 (.D(undriven), .en(and_20_out), .clk(clock), .Q(register_20_q));  // open: clr
  and and_20 (and_20_out, decoder_1_out20, RegWrite);
  Register #(.width(32)) register_21 (.D(undriven), .en(and_21_out), .clk(clock), .Q(register_21_q));  // open: clr
  and and_21 (and_21_out, decoder_1_out21, RegWrite);
  Register #(.width(32)) register_22 (.D(undriven), .en(and_22_out), .clk(clock), .Q(register_22_q));  // open: clr
  and and_22 (and_22_out, decoder_1_out22, RegWrite);
  Register #(.width(32)) register_23 (.D(undriven), .en(and_23_out), .clk(clock), .Q(register_23_q));  // open: clr
  and and_23 (and_23_out, decoder_1_out23, RegWrite);
  Register #(.width(32)) register_24 (.D(undriven), .en(and_24_out), .clk(clock), .Q(register_24_q));  // open: clr
  and and_24 (and_24_out, decoder_1_out24, RegWrite);
  Register #(.width(32)) register_25 (.D(undriven), .en(and_25_out), .clk(clock), .Q(register_25_q));  // open: clr
  and and_25 (and_25_out, decoder_1_out25, RegWrite);
  Register #(.width(32)) register_26 (.D(undriven), .en(and_26_out), .clk(clock), .Q(register_26_q));  // open: clr
  and and_26 (and_26_out, decoder_1_out26, RegWrite);
  Register #(.width(32)) register_27 (.D(undriven), .en(and_27_out), .clk(clock), .Q(register_27_q));  // open: clr
  and and_27 (and_27_out, decoder_1_out27, RegWrite);
  Register #(.width(32)) register_28 (.D(undriven), .en(and_28_out), .clk(clock), .Q(register_28_q));  // open: clr
  and and_28 (and_28_out, decoder_1_out28, RegWrite);
  Register #(.width(32)) register_29 (.D(undriven), .en(and_29_out), .clk(clock), .Q(register_29_q));  // open: clr
  and and_29 (and_29_out, decoder_1_out29, RegWrite);
  Register #(.width(32)) register_30 (.D(undriven), .en(and_30_out), .clk(clock), .Q(register_30_q));  // open: clr
  and and_30 (and_30_out, decoder_1_out30, RegWrite);
  Register #(.width(32)) register_31 (.D(undriven), .en(and_31_out), .clk(clock), .Q(register_31_q));  // open: clr
  and and_31 (and_31_out, decoder_1_out31, RegWrite);
  Decoder #(.enable("false"), .select(5)) decoder_2 (
    .out0(decoder_2_out0), .out1(decoder_2_out1), .out2(decoder_2_out2), .out3(decoder_2_out3),
    .out4(decoder_2_out4), .out5(decoder_2_out5), .out6(decoder_2_out6), .out7(decoder_2_out7),
    .out8(decoder_2_out8), .out9(decoder_2_out9), .out10(decoder_2_out10), .out11(decoder_2_out11),
    .out12(decoder_2_out12), .out13(decoder_2_out13), .out14(decoder_2_out14), .out15(decoder_2_out15),
    .out16(decoder_2_out16), .out17(decoder_2_out17), .out18(decoder_2_out18), .out19(decoder_2_out19),
    .out20(decoder_2_out20), .out21(decoder_2_out21), .out22(decoder_2_out22), .out23(decoder_2_out23),
    .out24(decoder_2_out24), .out25(decoder_2_out25), .out26(decoder_2_out26), .out27(decoder_2_out27),
    .out28(decoder_2_out28), .out29(decoder_2_out29), .out30(decoder_2_out30), .out31(decoder_2_out31),
    .sel(RA));
  assign controlled_buffer_1_out = decoder_2_out2 ? register_2_q : 32'bz;  // Controlled_Buffer controlled_buffer_1
  assign controlled_buffer_1_out = decoder_2_out3 ? register_3_q : 32'bz;  // Controlled_Buffer controlled_buffer_2
  assign controlled_buffer_1_out = decoder_2_out4 ? register_4_q : 32'bz;  // Controlled_Buffer controlled_buffer_3
  assign controlled_buffer_1_out = decoder_2_out5 ? register_5_q : 32'bz;  // Controlled_Buffer controlled_buffer_4
  assign controlled_buffer_1_out = decoder_2_out6 ? register_6_q : 32'bz;  // Controlled_Buffer controlled_buffer_5
  assign controlled_buffer_1_out = decoder_2_out7 ? register_7_q : 32'bz;  // Controlled_Buffer controlled_buffer_6
  assign controlled_buffer_1_out = decoder_2_out8 ? register_8_q : 32'bz;  // Controlled_Buffer controlled_buffer_7
  assign controlled_buffer_1_out = decoder_2_out9 ? register_9_q : 32'bz;  // Controlled_Buffer controlled_buffer_8
  assign controlled_buffer_1_out = decoder_2_out10 ? register_10_q : 32'bz;  // Controlled_Buffer controlled_buffer_9
  assign controlled_buffer_1_out = decoder_2_out11 ? register_11_q : 32'bz;  // Controlled_Buffer controlled_buffer_10
  assign controlled_buffer_1_out = decoder_2_out12 ? register_12_q : 32'bz;  // Controlled_Buffer controlled_buffer_11
  assign controlled_buffer_1_out = decoder_2_out13 ? register_13_q : 32'bz;  // Controlled_Buffer controlled_buffer_12
  assign controlled_buffer_1_out = decoder_2_out14 ? register_14_q : 32'bz;  // Controlled_Buffer controlled_buffer_13
  assign controlled_buffer_1_out = decoder_2_out15 ? register_15_q : 32'bz;  // Controlled_Buffer controlled_buffer_14
  assign controlled_buffer_1_out = decoder_2_out16 ? register_16_q : 32'bz;  // Controlled_Buffer controlled_buffer_15
  assign controlled_buffer_1_out = decoder_2_out17 ? register_17_q : 32'bz;  // Controlled_Buffer controlled_buffer_16
  assign controlled_buffer_1_out = decoder_2_out18 ? register_18_q : 32'bz;  // Controlled_Buffer controlled_buffer_17
  assign controlled_buffer_1_out = decoder_2_out19 ? register_19_q : 32'bz;  // Controlled_Buffer controlled_buffer_18
  assign controlled_buffer_1_out = decoder_2_out20 ? register_20_q : 32'bz;  // Controlled_Buffer controlled_buffer_19
  assign controlled_buffer_1_out = decoder_2_out21 ? register_21_q : 32'bz;  // Controlled_Buffer controlled_buffer_20
  assign controlled_buffer_1_out = decoder_2_out22 ? register_22_q : 32'bz;  // Controlled_Buffer controlled_buffer_21
  assign controlled_buffer_1_out = decoder_2_out23 ? register_23_q : 32'bz;  // Controlled_Buffer controlled_buffer_22
  assign controlled_buffer_1_out = decoder_2_out24 ? register_24_q : 32'bz;  // Controlled_Buffer controlled_buffer_23
  assign controlled_buffer_1_out = decoder_2_out25 ? register_25_q : 32'bz;  // Controlled_Buffer controlled_buffer_24
  assign controlled_buffer_1_out = decoder_2_out26 ? register_26_q : 32'bz;  // Controlled_Buffer controlled_buffer_25
  assign controlled_buffer_1_out = decoder_2_out27 ? register_27_q : 32'bz;  // Controlled_Buffer controlled_buffer_26
  assign controlled_buffer_1_out = decoder_2_out28 ? register_28_q : 32'bz;  // Controlled_Buffer controlled_buffer_27
  assign controlled_buffer_1_out = decoder_2_out29 ? register_29_q : 32'bz;  // Controlled_Buffer controlled_buffer_28
  assign controlled_buffer_1_out = decoder_2_out30 ? register_30_q : 32'bz;  // Controlled_Buffer controlled_buffer_29
  assign controlled_buffer_1_out = decoder_2_out31 ? register_31_q : 32'bz;  // Controlled_Buffer controlled_buffer_30
  assign controlled_buffer_1_out = decoder_2_out0 ? {32{1'b0}} : 32'bz;  // Controlled_Buffer controlled_buffer_31
  assign controlled_buffer_1_out = decoder_2_out1 ? register_1_q : 32'bz;  // Controlled_Buffer controlled_buffer_32
  Decoder #(.enable("false"), .select(5)) decoder_3 (
    .out0(decoder_3_out0), .out1(decoder_3_out1), .out2(decoder_3_out2), .out3(decoder_3_out3),
    .out4(decoder_3_out4), .out5(decoder_3_out5), .out6(decoder_3_out6), .out7(decoder_3_out7),
    .out8(decoder_3_out8), .out9(decoder_3_out9), .out10(decoder_3_out10), .out11(decoder_3_out11),
    .out12(decoder_3_out12), .out13(decoder_3_out13), .out14(decoder_3_out14), .out15(decoder_3_out15),
    .out16(decoder_3_out16), .out17(decoder_3_out17), .out18(decoder_3_out18), .out19(decoder_3_out19),
    .out20(decoder_3_out20), .out21(decoder_3_out21), .out22(decoder_3_out22), .out23(decoder_3_out23),
    .out24(decoder_3_out24), .out25(decoder_3_out25), .out26(decoder_3_out26), .out27(decoder_3_out27),
    .out28(decoder_3_out28), .out29(decoder_3_out29), .out30(decoder_3_out30), .out31(decoder_3_out31),
    .sel(RB));
  assign controlled_buffer_33_out = decoder_3_out0 ? {32{1'b0}} : 32'bz;  // Controlled_Buffer controlled_buffer_33
  assign controlled_buffer_33_out = decoder_3_out1 ? register_1_q : 32'bz;  // Controlled_Buffer controlled_buffer_34
  assign controlled_buffer_33_out = decoder_3_out2 ? register_2_q : 32'bz;  // Controlled_Buffer controlled_buffer_35
  assign controlled_buffer_33_out = decoder_3_out3 ? register_3_q : 32'bz;  // Controlled_Buffer controlled_buffer_36
  assign controlled_buffer_33_out = decoder_3_out4 ? register_4_q : 32'bz;  // Controlled_Buffer controlled_buffer_37
  assign controlled_buffer_33_out = decoder_3_out5 ? register_5_q : 32'bz;  // Controlled_Buffer controlled_buffer_38
  assign controlled_buffer_33_out = decoder_3_out6 ? register_6_q : 32'bz;  // Controlled_Buffer controlled_buffer_39
  assign controlled_buffer_33_out = decoder_3_out7 ? register_7_q : 32'bz;  // Controlled_Buffer controlled_buffer_40
  assign controlled_buffer_33_out = decoder_3_out8 ? register_8_q : 32'bz;  // Controlled_Buffer controlled_buffer_41
  assign controlled_buffer_33_out = decoder_3_out9 ? register_9_q : 32'bz;  // Controlled_Buffer controlled_buffer_42
  assign controlled_buffer_33_out = decoder_3_out10 ? register_10_q : 32'bz;  // Controlled_Buffer controlled_buffer_43
  assign controlled_buffer_33_out = decoder_3_out11 ? register_11_q : 32'bz;  // Controlled_Buffer controlled_buffer_44
  assign controlled_buffer_33_out = decoder_3_out12 ? register_12_q : 32'bz;  // Controlled_Buffer controlled_buffer_45
  assign controlled_buffer_33_out = decoder_3_out13 ? register_13_q : 32'bz;  // Controlled_Buffer controlled_buffer_46
  assign controlled_buffer_33_out = decoder_3_out14 ? register_14_q : 32'bz;  // Controlled_Buffer controlled_buffer_47
  assign controlled_buffer_33_out = decoder_3_out15 ? register_15_q : 32'bz;  // Controlled_Buffer controlled_buffer_48
  assign controlled_buffer_33_out = decoder_3_out16 ? register_16_q : 32'bz;  // Controlled_Buffer controlled_buffer_49
  assign controlled_buffer_33_out = decoder_3_out17 ? register_17_q : 32'bz;  // Controlled_Buffer controlled_buffer_50
  assign controlled_buffer_33_out = decoder_3_out18 ? register_18_q : 32'bz;  // Controlled_Buffer controlled_buffer_51
  assign controlled_buffer_33_out = decoder_3_out19 ? register_19_q : 32'bz;  // Controlled_Buffer controlled_buffer_52
  assign controlled_buffer_33_out = decoder_3_out20 ? register_20_q : 32'bz;  // Controlled_Buffer controlled_buffer_53
  assign controlled_buffer_33_out = decoder_3_out21 ? register_21_q : 32'bz;  // Controlled_Buffer controlled_buffer_54
  assign controlled_buffer_33_out = decoder_3_out22 ? register_22_q : 32'bz;  // Controlled_Buffer controlled_buffer_55
  assign controlled_buffer_33_out = decoder_3_out23 ? register_23_q : 32'bz;  // Controlled_Buffer controlled_buffer_56
  assign controlled_buffer_33_out = decoder_3_out24 ? register_24_q : 32'bz;  // Controlled_Buffer controlled_buffer_57
  assign controlled_buffer_33_out = decoder_3_out25 ? register_25_q : 32'bz;  // Controlled_Buffer controlled_buffer_58
  assign controlled_buffer_33_out = decoder_3_out26 ? register_26_q : 32'bz;  // Controlled_Buffer controlled_buffer_59
  assign controlled_buffer_33_out = decoder_3_out27 ? register_27_q : 32'bz;  // Controlled_Buffer controlled_buffer_60
  assign controlled_buffer_33_out = decoder_3_out28 ? register_28_q : 32'bz;  // Controlled_Buffer controlled_buffer_61
  assign controlled_buffer_33_out = decoder_3_out29 ? register_29_q : 32'bz;  // Controlled_Buffer controlled_buffer_62
  assign controlled_buffer_33_out = decoder_3_out30 ? register_30_q : 32'bz;  // Controlled_Buffer controlled_buffer_63
  assign controlled_buffer_33_out = decoder_3_out31 ? register_31_q : 32'bz;  // Controlled_Buffer controlled_buffer_64
endmodule

module ALU (
  input  [31:0] A,
  input  [31:0] B,
  input  [11:0] ALUop,
  output [31:0] Result,
  output Branch
);

  wire comparator_1_eq, comparator_1_lt, comparator_2_lt, multiplexer_4_out, not_3_out, not_4_out, not_5_out;
  wire [31:0] adder_1_out, and_1_out, bit_extender_1_out, multiplexer_1_out, multiplexer_2_out,
       multiplexer_3_out, multiplier_1_out, not_1_out, not_2_out, or_1_out, shifter_1_out, shifter_2_out,
       shifter_3_out, shifter_4_out, xor_1_out;

  assign not_1_out = ~A;  // NOT_Gate not_1, 32 bits wide
  assign not_2_out = ~B;  // NOT_Gate not_2, 32 bits wide
  Multiplexer #(.width(32)) multiplexer_1 (.in0(A), .in1(not_1_out), .out(multiplexer_1_out), .sel(ALUop[0]));
  Multiplexer #(.width(32)) multiplexer_2 (.in0(B), .in1(not_2_out), .out(multiplexer_2_out), .sel(ALUop[1]));
  Shifter #(.width(32)) shifter_1 (.in(multiplexer_1_out), .\dist (multiplexer_2_out[4:0]), .out(shifter_1_out));
  Shifter #(.shift("lr"), .width(32)) shifter_2 (
    .in(multiplexer_1_out), .\dist (multiplexer_2_out[4:0]), .out(shifter_2_out));
  Shifter #(.shift("ar"), .width(32)) shifter_3 (
    .in(multiplexer_1_out), .\dist (multiplexer_2_out[4:0]), .out(shifter_3_out));
  Shifter #(.shift("rr"), .width(32)) shifter_4 (
    .in(multiplexer_1_out), .\dist (multiplexer_2_out[4:0]), .out(shifter_4_out));
  assign xor_1_out = multiplexer_1_out ^ multiplexer_2_out;  // XOR_Gate xor_1, 32 bits wide
  assign or_1_out = multiplexer_1_out | multiplexer_2_out;  // OR_Gate or_1, 32 bits wide
  assign and_1_out = multiplexer_1_out & multiplexer_2_out;  // AND_Gate and_1, 32 bits wide
  Multiplier #(.width(32)) multiplier_1 (
    .a(multiplexer_1_out), .b(multiplexer_2_out), .out(multiplier_1_out));  // open: cin, cout
  Adder #(.width(32)) adder_1 (
    .a(multiplexer_1_out), .b(multiplexer_2_out), .out(adder_1_out), .cin(ALUop[1]));  // open: cout
  Comparator #(.width(32)) comparator_1 (.a(A), .b(B), .eq(comparator_1_eq), .lt(comparator_1_lt));  // open: gt
  Comparator #(.mode("unsigned"), .width(32)) comparator_2 (.a(A), .b(B), .lt(comparator_2_lt));  // open: gt, eq
  not not_3 (not_3_out, comparator_1_lt);
  not not_4 (not_4_out, comparator_1_eq);
  not not_5 (not_5_out, comparator_2_lt);
  Multiplexer #(.select(2), .width(32)) multiplexer_3 (
    .in0(shifter_1_out), .in1(shifter_2_out), .in2(shifter_3_out), .in3(shifter_4_out),
    .out(multiplexer_3_out), .sel(ALUop[3:2]));
  assign bit_extender_1_out = {{31{1'b0}}, multiplexer_4_out};  // Bit_Extender bit_extender_1
  Multiplexer #(.select(2)) multiplexer_4 (
    .in0(comparator_1_eq), .in1(comparator_1_lt), .in2(comparator_2_lt), .out(multiplexer_4_out),
    .sel(ALUop[5:4]));  // open: in3
  Multiplexer #(.select(3)) multiplexer_5 (
    .in0(1'b0), .in1(comparator_1_lt), .in2(not_3_out), .in3(comparator_1_eq), .in4(not_4_out),
    .in5(comparator_2_lt), .in6(not_5_out), .out(Branch), .sel(ALUop[8:6]));  // open: in7
  Multiplexer #(.select(3), .width(32)) multiplexer_6 (
    .in0(multiplexer_3_out), .in1(adder_1_out), .in2(bit_extender_1_out), .in3(xor_1_out), .in4(or_1_out),
    .in5(and_1_out), .in6(multiplier_1_out), .out(Result), .sel(ALUop[11:9]));  // open: in7

  // Other names for the same wires on the sheet: Ainvert = ALUop[0]; Binvert = ALUop[1]; ShiftOp[1:0] = ALUop[3:2];
  //   SetOp[1:0] = ALUop[5:4]; BranchOp[2:0] = ALUop[8:6]; ALUop_t[2:0] = ALUop[11:9]
endmodule

module ALUcontrol (
  input  [10:0] func,
  input  [5:0] OPcode,
  output [11:0] ALUop
);

  wire and_2_out, and_3_out, and_4_out, and_5_out, and_6_out, and_7_out, and_8_out, and_9_out, and_10_out,
       and_11_out, and_14_out, and_15_out, and_16_out, and_17_out, and_18_out, and_19_out, and_20_out,
       and_21_out, and_22_out, and_23_out, and_24_out, and_25_out, and_26_out, and_27_out, not_2_out,
       not_3_out, not_4_out, not_6_out, not_7_out, S;
  wire [11:0] FuncOut, OpCodeOut;

  not not_1 (FuncOut[4], func[3]);
  not not_2 (not_2_out, func[2]);
  not not_3 (not_3_out, func[1]);
  not not_4 (not_4_out, func[0]);
  and and_1 (FuncOut[0], func[3], func[2], not_4_out);
  and and_2 (and_2_out, FuncOut[4], func[2], not_3_out, func[0]);
  and and_3 (and_3_out, func[3], func[2], not_4_out);
  and and_4 (and_4_out, func[3], func[1]);
  and and_5 (and_5_out, func[3], func[2]);
  and and_6 (and_6_out, func[2], func[1]);
  and and_7 (and_7_out, func[3], not_2_out, not_3_out);
  and and_8 (and_8_out, func[3], not_3_out, func[0]);
  and and_9 (and_9_out, FuncOut[4], func[2], not_3_out);
  and and_10 (and_10_out, func[3], not_2_out, func[0]);
  and and_11 (and_11_out, func[2], not_3_out, not_4_out);
  or or_1 (FuncOut[1], and_2_out, and_3_out);
  or or_2 (FuncOut[11], and_4_out, and_5_out);
  or or_3 (FuncOut[10], and_6_out, and_7_out, and_8_out);
  or or_4 (FuncOut[9], and_9_out, and_10_out, and_11_out);
  or or_5 (S, OPcode[0], OPcode[1], OPcode[2], OPcode[3], OPcode[4], OPcode[5]);
  not not_5 (OpCodeOut[4], OPcode[3]);
  not not_6 (not_6_out, OPcode[2]);
  not not_7 (not_7_out, OPcode[1]);
  not not_8 (OpCodeOut[2], OPcode[0]);
  and and_12 (OpCodeOut[0], OPcode[3], OPcode[2], not_7_out, OpCodeOut[2]);
  and and_13 (OpCodeOut[1], OPcode[3], OPcode[2], not_7_out, OpCodeOut[2]);
  and and_14 (and_14_out, OPcode[1], OPcode[0]);
  and and_15 (and_15_out, OPcode[4], OPcode[1], OPcode[0]);
  and and_16 (and_16_out, OPcode[4], OPcode[2], OPcode[1]);
  and and_17 (and_17_out, OPcode[4], not_6_out, OPcode[1], OpCodeOut[2]);
  and and_18 (and_18_out, OPcode[4], OPcode[2], OPcode[0]);
  and and_19 (and_19_out, OPcode[4], OPcode[1], OpCodeOut[2]);
  and and_20 (and_20_out, OPcode[4], OPcode[2], OpCodeOut[2]);
  and and_21 (and_21_out, OPcode[3], not_6_out, OPcode[1]);
  and and_22 (and_22_out, OPcode[3], OPcode[2], not_7_out, OpCodeOut[2]);
  and and_23 (and_23_out, OpCodeOut[4], OPcode[2], OPcode[1]);
  and and_24 (and_24_out, OPcode[3], not_6_out, not_7_out);
  and and_25 (and_25_out, OPcode[2], not_7_out, OPcode[0]);
  and and_26 (and_26_out, OPcode[3], OPcode[0]);
  and and_27 (and_27_out, OPcode[3], OPcode[2]);
  or or_6 (OpCodeOut[3], and_14_out, OPcode[2]);
  or or_7 (OpCodeOut[8], and_15_out, and_16_out);
  or or_8 (OpCodeOut[7], and_17_out, and_18_out);
  or or_9 (OpCodeOut[6], and_19_out, and_20_out);
  or or_10 (OpCodeOut[11], and_21_out, and_22_out);
  or or_11 (OpCodeOut[10], and_23_out, and_24_out);
  or or_12 (OpCodeOut[9], and_25_out, and_26_out, and_27_out, OPcode[4]);
  Multiplexer #(.width(12)) multiplexer_1 (
    .in0({FuncOut[11:9], 3'b000, func[0], FuncOut[4], func[1:0], FuncOut[1:0]}),
    .in1({OpCodeOut[11:6], OPcode[0], OpCodeOut[4:0]}), .out(ALUop), .sel(S));

  // Other names for the same wires on the sheet: FuncOut (some bits) = {func[0], func[1:0]}; OpCodeOut[5] = OPcode[0]
endmodule

module PC (
  input  [31:0] NextPC32,
  input  [19:0] PC20,
  input  [19:0] JALRPC,
  input  [10:0] ImmU11,
  input  [1:0] PCSrc,
  input  Clock,
  input  [4:0] ImmL5
);

  wire [19:0] adder_1_out, adder_2_out, bit_extender_1_out, multiplexer_1_out;

  Multiplexer #(.select(2), .width(20)) multiplexer_1 (
    .in0(adder_1_out), .in1(adder_2_out), .in2(JALRPC), .out(multiplexer_1_out), .sel(PCSrc));  // open: in3
  Register #(.width(20)) ProgramCounter (.D(multiplexer_1_out), .en(1'b1), .clk(Clock), .Q(PC20));  // open: clr
  Adder #(.width(20)) adder_1 (.a(PC20), .b(20'h1), .out(adder_1_out));  // open: cin, cout
  assign bit_extender_1_out = {{4{ImmL5[4]}}, {ImmL5, ImmU11}};  // Bit_Extender bit_extender_1
  Adder #(.width(20)) adder_2 (.a(adder_1_out), .b(bit_extender_1_out), .out(adder_2_out));  // open: cin, cout
  assign NextPC32 = {{12{adder_1_out[19]}}, adder_1_out};  // Bit_Extender bit_extender_2
endmodule

module instruction_memory (
  input  [19:0] in_1,
  output [5:0] out_2,
  output [4:0] out_3,
  output [4:0] out_4,
  output [4:0] out_5,
  output [4:0] out_6,
  output [5:0] out_7
);

  ROM #(.addrWidth(20), .dataWidth(32)) rom_1 (.addr(in_1), .data({out_7, out_6, out_5, out_4, out_3, out_2}));

  // Notes on the sheet:
  //   contents of rom_1 (hex, n*v repeats v):
  //   5*0 100000 0 0 0 1000000 0 0 0 1100000 0 0 0 10000000 0 0 0 10100000 0 0 0 11000000 0 0 0 11100000 0
  //   0 1 0 0 0 1 100000 0 0 1 1000000 0 0 1 1100000 0 0 1 10000000 0 0 1 10100000 5*0 1 0 0 0 10 0 0 0 11
  //   0 0 0 100 0 0 0 101 0 0 0 110 0 0 0 111 0 0 0 1000 0 0 0 1001 0 0 0 1010 0 0 0 1011 0 0 0 1100 0 0 0
  //   1101 0 0 0 1110 0 0 0 1111 0 0 0 10000 0 0 0 10001 0 0 0 10010 0 0 0 10011 0 0 0 10100 0 0 0 10101 0
  //   0 0 10110 0 0 0 10111
endmodule

module data_memory (
  input  [19:0] in_1,
  input  [31:0] in_2,
  input  in_3,
  input  in_4,
  input  in_5,
  output [31:0] out_6
);

  RAM #(.addrWidth(20), .dataWidth(32)) ram_1 (.addr(in_1), .we(in_3), .oe(in_4), .clk(in_5), .din(in_2), .dout(out_6));
endmodule

module ExtendUnit (
  input  ExtendOp,
  input  [15:0] in_2,
  output [31:0] out_3
);

  wire [31:0] bit_extender_1_out, bit_extender_2_out;

  assign bit_extender_1_out = {{16{in_2[15]}}, in_2};  // Bit_Extender bit_extender_1
  Multiplexer #(.width(32)) multiplexer_1 (
    .in0(bit_extender_1_out), .in1(bit_extender_2_out), .out(out_3), .sel(ExtendOp));
  assign bit_extender_2_out = {{16{1'b0}}, in_2};  // Bit_Extender bit_extender_2
endmodule

module naruhodo (
  input  [5:0] OPcode
);

  wire Ainvert, and_3_out, and_4_out, and_5_out, and_6_out, and_7_out, and_8_out, and_9_out, and_10_out,
       and_11_out, and_12_out, and_13_out, and_14_out, and_15_out, and_16_out, Binvert, not_2_out, not_3_out;
  wire [0:0] SetOp;
  wire [1:0] ShiftOp;
  wire [2:0] ALUop, BranchOp;

  not not_1 (SetOp[0], OPcode[3]);
  not not_2 (not_2_out, OPcode[2]);
  not not_3 (not_3_out, OPcode[1]);
  not not_4 (ShiftOp[0], OPcode[0]);
  and and_1 (Ainvert, OPcode[3], OPcode[2], not_3_out, ShiftOp[0]);
  and and_2 (Binvert, OPcode[3], OPcode[2], not_3_out, ShiftOp[0]);
  and and_3 (and_3_out, OPcode[1], OPcode[0]);
  and and_4 (and_4_out, OPcode[4], OPcode[1], OPcode[0]);
  and and_5 (and_5_out, OPcode[4], OPcode[2], OPcode[1]);
  and and_6 (and_6_out, OPcode[4], not_2_out, OPcode[1], ShiftOp[0]);
  and and_7 (and_7_out, OPcode[4], OPcode[2], OPcode[0]);
  and and_8 (and_8_out, OPcode[4], OPcode[1], ShiftOp[0]);
  and and_9 (and_9_out, OPcode[4], OPcode[2], ShiftOp[0]);
  and and_10 (and_10_out, OPcode[3], not_2_out, OPcode[1]);
  and and_11 (and_11_out, OPcode[3], OPcode[2], not_3_out, ShiftOp[0]);
  and and_12 (and_12_out, SetOp[0], OPcode[2], OPcode[1]);
  and and_13 (and_13_out, OPcode[3], not_2_out, not_3_out);
  and and_14 (and_14_out, OPcode[2], not_3_out, OPcode[0]);
  and and_15 (and_15_out, OPcode[3], OPcode[0]);
  and and_16 (and_16_out, OPcode[3], OPcode[2]);
  or or_1 (ShiftOp[1], and_3_out, OPcode[2]);
  or or_2 (BranchOp[2], and_4_out, and_5_out);
  or or_3 (BranchOp[1], and_6_out, and_7_out);
  or or_4 (BranchOp[0], and_8_out, and_9_out);
  or or_5 (ALUop[2], and_10_out, and_11_out);
  or or_6 (ALUop[1], and_12_out, and_13_out);
  or or_7 (ALUop[0], and_14_out, and_15_out, and_16_out, OPcode[4]);

  // Other names for the same wires on the sheet: SetOp[1] = OPcode[0]
endmodule
